# Fritzing sketch wiring (saved by Fritzing 0.9.0b)
breadboards: 1

parts:
  Part1 = Photon
  T1 = LM35 Temperature Sensor [package="TO92 [THT]"]

nets:
  N1: Part1.A0, T1.Vout
  GND: Part1.GND, T1.GND
  N2: Part1.VIN, T1.+Vs
